// Logisim project alu.circ as structural Verilog: 21 circuits, main circuit main
module main (
  input  [7:0] A,
  input  [7:0] B,
  input  Add_Sub,
  input  [3:0] in_4,
  input  Shift_in,
  input  Shift_in_2,
  output [7:0] Output,
  output Overflow,
  output A_B,
  output A_B_2,
  output A_B_3,
  output Shift_out,
  output Shift_out_2
);

  wire [7:0] A_1_2_output, A_1_output, adder_8bit_1_output, and_8bit_1_and,
       comparator_8bit_splitter_1_output, NOT_A_out_2, or_8bit_1_and, Shift_left_output, Shift_Right_output,
       xor_8bit_1_and;

  NOT_8it NOT_A (.i(A), .out_2(NOT_A_out_2));
  AND_8bit and_8bit_1 (.A(A), .B(B), .AND(and_8bit_1_and));
  OR_8bit or_8bit_1 (.A(A), .B(B), .AND(or_8bit_1_and));
  XOR_8bit xor_8bit_1 (.A(A), .B(B), .AND(xor_8bit_1_and));
  Adder_8bit adder_8bit_1 (.Cout(Overflow), .A(A), .B(B), .Output(adder_8bit_1_output), .ADD_SUB_toggle(Add_Sub));
  Incrementer_8bit A_1 (.Input(A), .Output(A_1_output));
  Decrementer_8bit A_1_2 (.Input(A), .Output(A_1_2_output));
  comparator_8bit_splitter comparator_8bit_splitter_1 (
    .A(A), .B(B), .Output(comparator_8bit_splitter_1_output), .A_B(A_B), .A_B_2(A_B_2), .A_B_3(A_B_3));
  shifter_right Shift_Right (.\input (A), .shift_out(Shift_out), .shift_in(Shift_in), .\output (Shift_Right_output));
  shifter_left Shift_left (.\input (A), .shift_in(Shift_in_2), .shift_out(Shift_out_2), .\output (Shift_left_output));
  Multiplexer #(.select(4), .width(8), .enable("false")) multiplexer_1 (
    .in0(NOT_A_out_2), .in1(and_8bit_1_and), .in2(or_8bit_1_and), .in3(xor_8bit_1_and),
    .in4(adder_8bit_1_output), .in5(A_1_output), .in6(A_1_2_output), .in7(comparator_8bit_splitter_1_output),
    .in8(Shift_Right_output), .in9(Shift_left_output), .out(Output), .sel(in_4));  // open: in10, in11, in12, in13, in14, in15
  Hex_Digit_Display hex_digit_display_1 (.value(Output[7:4]));  // open: dp
  Hex_Digit_Display hex_digit_display_2 (.value(Output[3:0]));  // open: dp
endmodule

// AND
module AND_8bit (
  input  [7:0] A,
  input  [7:0] B,
  output [7:0] AND
);

  and and_1 (AND[0], A[0], B[0]);
  and and_2 (AND[1], A[1], B[1]);
  and and_3 (AND[2], A[2], B[2]);
  and and_4 (AND[3], A[3], B[3]);
  and and_5 (AND[4], A[4], B[4]);
  and and_6 (AND[5], A[5], B[5]);
  and and_7 (AND[6], A[6], B[6]);
  and and_8 (AND[7], A[7], B[7]);
endmodule

// OR
module OR_8bit (
  input  [7:0] A,
  input  [7:0] B,
  output [7:0] AND
);

  or or_1 (AND[0], A[0], B[0]);
  or or_2 (AND[1], A[1], B[1]);
  or or_3 (AND[2], A[2], B[2]);
  or or_4 (AND[3], A[3], B[3]);
  or or_5 (AND[4], A[4], B[4]);
  or or_6 (AND[5], A[5], B[5]);
  or or_7 (AND[6], A[6], B[6]);
  or or_8 (AND[7], A[7], B[7]);
endmodule

// XOR
module XOR_8bit (
  input  [7:0] A,
  input  [7:0] B,
  output [7:0] AND
);

  xor XOR (AND[0], A[0], B[0]);
  xor XOR_2 (AND[1], A[1], B[1]);
  xor XOR_3 (AND[2], A[2], B[2]);
  xor XOR_4 (AND[3], A[3], B[3]);
  xor XOR_5 (AND[4], A[4], B[4]);
  xor XOR_6 (AND[5], A[5], B[5]);
  xor XOR_7 (AND[6], A[6], B[6]);
  xor XOR_8 (AND[7], A[7], B[7]);
endmodule

module Half_Adder (
  input  A,
  input  B,
  output S,
  output C
);

  xor xor_1 (S, A, B);
  and and_1 (C, A, B);
endmodule

// +/-
module Adder_8bit (
  input  ADD_SUB_toggle,
  input  [7:0] B,
  input  [7:0] A,
  output Cout,
  output [7:0] Output
);

  wire full_adder1bit_2_cout, full_adder1bit_3_cout, full_adder1bit_4_cout, full_adder1bit_5_cout,
       full_adder1bit_6_cout, full_adder1bit_7_cout, full_adder1bit_8_cout;
  wire [7:0] xor_8bit_toggle_1_output;

  Full_Adder1bit full_adder1bit_1 (
    .Cin(full_adder1bit_2_cout), .Sum(Output[7]), .B(xor_8bit_toggle_1_output[7]), .A(A[7]), .Cout(Cout));
  Full_Adder1bit full_adder1bit_2 (
    .Cin(full_adder1bit_3_cout), .Sum(Output[6]), .B(xor_8bit_toggle_1_output[6]), .A(A[6]),
    .Cout(full_adder1bit_2_cout));
  Full_Adder1bit full_adder1bit_3 (
    .Cin(full_adder1bit_4_cout), .Sum(Output[5]), .B(xor_8bit_toggle_1_output[5]), .A(A[5]),
    .Cout(full_adder1bit_3_cout));
  Full_Adder1bit full_adder1bit_4 (
    .Cin(full_adder1bit_5_cout), .Sum(Output[4]), .B(xor_8bit_toggle_1_output[4]), .A(A[4]),
    .Cout(full_adder1bit_4_cout));
  Full_Adder1bit full_adder1bit_5 (
    .Cin(full_adder1bit_6_cout), .Sum(Output[3]), .B(xor_8bit_toggle_1_output[3]), .A(A[3]),
    .Cout(full_adder1bit_5_cout));
  Full_Adder1bit full_adder1bit_6 (
    .Cin(full_adder1bit_7_cout), .Sum(Output[2]), .B(xor_8bit_toggle_1_output[2]), .A(A[2]),
    .Cout(full_adder1bit_6_cout));
  Full_Adder1bit full_adder1bit_7 (
    .Cin(full_adder1bit_8_cout), .Sum(Output[1]), .B(xor_8bit_toggle_1_output[1]), .A(A[1]),
    .Cout(full_adder1bit_7_cout));
  Full_Adder1bit full_adder1bit_8 (
    .Cin(ADD_SUB_toggle), .Sum(Output[0]), .B(xor_8bit_toggle_1_output[0]), .A(A[0]),
    .Cout(full_adder1bit_8_cout));
  XOR_8bit_toggle xor_8bit_toggle_1 (.Input(B), .Output(xor_8bit_toggle_1_output), .Toggle(ADD_SUB_toggle));
endmodule

module Full_Adder1bit (
  input  Cin,
  input  B,
  input  A,
  output Sum,
  output Cout
);

  wire half_adder_1_c, half_adder_1_s, half_adder_2_c;

  Half_Adder half_adder_1 (.A(A), .B(B), .S(half_adder_1_s), .C(half_adder_1_c));
  Half_Adder half_adder_2 (.A(half_adder_1_s), .B(Cin), .S(Sum), .C(half_adder_2_c));
  or or_1 (Cout, half_adder_2_c, half_adder_1_c);
endmodule

module XOR_8bit_toggle (
  input  [7:0] Input,
  input  Toggle,
  output [7:0] Output
);

  xor xor_1 (Output[7], Input[7], Toggle);
  xor xor_2 (Output[6], Input[6], Toggle);
  xor xor_3 (Output[4], Input[4], Toggle);
  xor xor_4 (Output[5], Input[5], Toggle);
  xor xor_5 (Output[3], Input[3], Toggle);
  xor xor_6 (Output[2], Input[2], Toggle);
  xor xor_7 (Output[1], Input[1], Toggle);
  xor xor_8 (Output[0], Input[0], Toggle);
endmodule

module Incrementer_8bit (
  input  [7:0] Input,
  output [7:0] Output
);

  Adder_8bit adder_8bit_1 (.A(8'h1), .B(Input), .Output(Output), .ADD_SUB_toggle(1'b0));  // open: Cout
endmodule

module Decrementer_8bit (
  input  [7:0] Input,
  output [7:0] Output
);

  Adder_8bit adder_8bit_1 (.A(Input), .B(8'h1), .Output(Output), .ADD_SUB_toggle(1'b1));  // open: Cout
endmodule

module Comparator_8bit (
  input  A7,
  input  A6,
  input  B7,
  input  B6,
  input  A5,
  input  A4,
  input  B5,
  input  B4,
  input  A3,
  input  A2,
  input  B3,
  input  B2,
  input  A1,
  input  A0,
  input  B1,
  input  B0,
  output A_B,
  output A_B_2,
  output A_B_3
);

  wire and_1_out, and_3_out, comparator_4bit_1_a_b, comparator_4bit_1_a_b_2, comparator_4bit_1_a_b_3,
       comparator_4bit_2_a_b, comparator_4bit_2_a_b_2, comparator_4bit_2_a_b_3;

  Comparator_4bit comparator_4bit_1 (
    .A3(A7), .A2(A6), .B3(B7), .B2(B6), .A1(A5), .A0(A4), .B1(B5), .B0(B4), .A_B(comparator_4bit_1_a_b),
    .A_B_2(comparator_4bit_1_a_b_2), .A_B_3(comparator_4bit_1_a_b_3));
  Comparator_4bit comparator_4bit_2 (
    .A3(A3), .A2(A2), .B3(B3), .B2(B2), .A1(A1), .A0(A0), .B1(B1), .B0(B0), .A_B(comparator_4bit_2_a_b),
    .A_B_2(comparator_4bit_2_a_b_2), .A_B_3(comparator_4bit_2_a_b_3));
  and and_1 (and_1_out, comparator_4bit_1_a_b_2, comparator_4bit_2_a_b);
  and and_2 (A_B_2, comparator_4bit_1_a_b_2, comparator_4bit_2_a_b_2);
  and and_3 (and_3_out, comparator_4bit_1_a_b_2, comparator_4bit_2_a_b_3);
  or or_1 (A_B, comparator_4bit_1_a_b, and_1_out);
  or or_2 (A_B_3, and_3_out, comparator_4bit_1_a_b_3);
endmodule

module Comparator_4bit (
  input  A3,
  input  A2,
  input  B3,
  input  B2,
  input  A1,
  input  A0,
  input  B1,
  input  B0,
  output A_B,
  output A_B_2,
  output A_B_3
);

  wire and_1_out, and_3_out, comparator_2bit_1_a_b, comparator_2bit_1_a_b_2, comparator_2bit_1_a_b_3,
       comparator_2bit_2_a_b, comparator_2bit_2_a_b_2, comparator_2bit_2_a_b_3;

  comparator_2bit comparator_2bit_1 (
    .A1(A3), .A0(A2), .B1(B3), .B0(B2), .A_B(comparator_2bit_1_a_b), .A_B_2(comparator_2bit_1_a_b_2),
    .A_B_3(comparator_2bit_1_a_b_3));
  comparator_2bit comparator_2bit_2 (
    .A1(A1), .A0(A0), .B1(B1), .B0(B0), .A_B(comparator_2bit_2_a_b), .A_B_2(comparator_2bit_2_a_b_2),
    .A_B_3(comparator_2bit_2_a_b_3));
  and and_1 (and_1_out, comparator_2bit_1_a_b_2, comparator_2bit_2_a_b);
  and and_2 (A_B_2, comparator_2bit_1_a_b_2, comparator_2bit_2_a_b_2);
  and and_3 (and_3_out, comparator_2bit_1_a_b_2, comparator_2bit_2_a_b_3);
  or or_1 (A_B, comparator_2bit_1_a_b, and_1_out);
  or or_2 (A_B_3, and_3_out, comparator_2bit_1_a_b_3);
endmodule

module comparator_2bit (
  input  A1,
  input  A0,
  input  B1,
  input  B0,
  output A_B,
  output A_B_2,
  output A_B_3
);

  wire and_1_out, and_2_out, and_3_out, and_4_out, and_5_out, and_6_out, not_1_out, not_2_out, not_3_out,
       not_4_out, not_5_out, not_6_out, xor_1_out, xor_2_out;

  not not_1 (not_1_out, A1);
  not not_2 (not_2_out, B1);
  not not_3 (not_3_out, A0);
  not not_4 (not_4_out, B0);
  and and_1 (and_1_out, not_1_out, B1);
  and and_2 (and_2_out, not_3_out, B1, B0);
  and and_3 (and_3_out, not_1_out, not_3_out, B0);
  xor xor_1 (xor_1_out, A0, B0);
  xor xor_2 (xor_2_out, A1, B1);
  and and_4 (and_4_out, A1, not_2_out);
  and and_5 (and_5_out, not_2_out, not_4_out, A0);
  and and_6 (and_6_out, A1, A0, not_4_out);
  not not_5 (not_5_out, xor_1_out);
  not not_6 (not_6_out, xor_2_out);
  or or_1 (A_B_3, and_1_out, and_2_out, and_3_out);
  and and_7 (A_B_2, not_5_out, not_6_out);
  or or_2 (A_B, and_4_out, and_5_out, and_6_out);
endmodule

module comparator_8bit_splitter (
  input  [7:0] A,
  input  [7:0] B,
  output [7:0] Output,
  output A_B,
  output A_B_2,
  output A_B_3
);

  Comparator_8bit comparator_8bit_1 (
    .A7(A[7]), .A6(A[6]), .B7(B[7]), .B6(B[6]), .A5(A[5]), .A4(A[4]), .B5(B[5]), .B4(B[4]), .A3(A[3]),
    .A2(A[2]), .B3(B[3]), .B2(B[2]), .A1(A[1]), .A0(A[0]), .B1(B[1]), .B0(B[0]), .A_B(A_B), .A_B_2(A_B_2),
    .A_B_3(A_B_3));

  assign Output[2:0] = {A_B_3, A_B_2, A_B};
endmodule

module register_8bit (
  input  [7:0] i,
  input  s,
  input  e,
  output [7:0] out_4,
  output [7:0] _0
);

  mem_8bit mem_8bit_1 (.in_1(i), .s(s), .out_3(out_4));
  enable_8bit enable_8bit_1 (.in_1(out_4), .in_2(e), .out_3(_0));
endmodule

// NOT
module NOT_8it (
  input  [7:0] i,
  output [7:0] out_2
);

  not not_1 (out_2[0], i[0]);
  not not_2 (out_2[1], i[1]);
  not not_3 (out_2[2], i[2]);
  not not_4 (out_2[3], i[3]);
  not not_5 (out_2[4], i[4]);
  not not_6 (out_2[5], i[5]);
  not not_7 (out_2[6], i[6]);
  not not_8 (out_2[7], i[7]);
endmodule

module shifter_right (
  input  [7:0] \input ,
  input  shift_in,
  output shift_out,
  output [7:0] \output 
);

  wire [7:1] register_8bit_1__0;

  register_8bit register_8bit_1 (.i(\input ), .s(1'b1), .e(1'b1), ._0({register_8bit_1__0, shift_out}));  // open: out_4
  register_8bit register_8bit_2 (.i({shift_in, register_8bit_1__0}), .s(1'b1), .e(1'b1), ._0(\output ));  // open: out_4
endmodule

module shifter_left (
  input  shift_in,
  input  [7:0] \input ,
  output [7:0] \output ,
  output shift_out
);

  wire [6:0] register_8bit_1__0;

  register_8bit register_8bit_1 (.i(\input ), .s(1'b1), .e(1'b1), ._0({shift_out, register_8bit_1__0}));  // open: out_4
  register_8bit register_8bit_2 (.i({register_8bit_1__0, shift_in}), .s(1'b1), .e(1'b1), ._0(\output ));  // open: out_4
endmodule

module mem_1bit (
  input  in_1,
  input  in_2,
  output out_3
);

  wire nand_1_out, nand_2_out, nand_4_out;

  nand nand_1 (nand_1_out, in_1, in_2);
  nand nand_2 (nand_2_out, nand_1_out, in_2);
  nand nand_3 (out_3, nand_1_out, nand_4_out);
  nand nand_4 (nand_4_out, out_3, nand_2_out);
endmodule

module mem_8bit (
  input  [7:0] in_1,
  input  s,
  output [7:0] out_3
);

  mem_1bit mem_1bit_1 (.in_1(in_1[0]), .in_2(s), .out_3(out_3[0]));
  mem_1bit mem_1bit_2 (.in_1(in_1[1]), .in_2(s), .out_3(out_3[1]));
  mem_1bit mem_1bit_3 (.in_1(in_1[2]), .in_2(s), .out_3(out_3[2]));
  mem_1bit mem_1bit_4 (.in_1(in_1[3]), .in_2(s), .out_3(out_3[3]));
  mem_1bit mem_1bit_5 (.in_1(in_1[4]), .in_2(s), .out_3(out_3[4]));
  mem_1bit mem_1bit_6 (.in_1(in_1[5]), .in_2(s), .out_3(out_3[5]));
  mem_1bit mem_1bit_7 (.in_1(in_1[6]), .in_2(s), .out_3(out_3[6]));
  mem_1bit mem_1bit_8 (.in_1(in_1[7]), .in_2(s), .out_3(out_3[7]));
endmodule

// EN
module enable_8bit (
  input  [7:0] in_1,
  input  in_2,
  output [7:0] out_3
);

  wire and_1_out, and_2_out, and_3_out, and_4_out, and_5_out, and_6_out, and_7_out, and_8_out;

  assign out_3[0] = in_2 ? and_1_out : 1'bz;  // Controlled_Buffer controlled_buffer_1
  and and_1 (and_1_out, in_1[0], in_2);
  assign out_3[1] = in_2 ? and_2_out : 1'bz;  // Controlled_Buffer controlled_buffer_2
  and and_2 (and_2_out, in_1[1], in_2);
  and and_3 (and_3_out, in_1[2], in_2);
  assign out_3[2] = in_2 ? and_3_out : 1'bz;  // Controlled_Buffer controlled_buffer_3
  and and_4 (and_4_out, in_1[3], in_2);
  assign out_3[3] = in_2 ? and_4_out : 1'bz;  // Controlled_Buffer controlled_buffer_4
  assign out_3[4] = in_2 ? and_5_out : 1'bz;  // Controlled_Buffer controlled_buffer_5
  and and_5 (and_5_out, in_1[4], in_2);
  assign out_3[5] = in_2 ? and_6_out : 1'bz;  // Controlled_Buffer controlled_buffer_6
  and and_6 (and_6_out, in_1[5], in_2);
  assign out_3[6] = in_2 ? and_7_out : 1'bz;  // Controlled_Buffer controlled_buffer_7
  and and_7 (and_7_out, in_1[6], in_2);
  assign out_3[7] = in_2 ? and_8_out : 1'bz;  // Controlled_Buffer controlled_buffer_8
  and and_8 (and_8_out, in_1[7], in_2);
endmodule
